// Logisim project CLA.circ as structural Verilog: 9 circuits, main circuit main
module main (
  input  [15:0] A,
  input  [15:0] B,
  input  [15:0] _1,
  input  S,
  output [15:0] Sum,
  output C_V
);

  wire [15:0] Complementer_y, Selector_out_4;

  _2_s_Complementer Complementer (.X(B), ._1(_1), .Y(Complementer_y));
  Selector Selector (.A(B), .B(Complementer_y), .Select(S), .out_4(Selector_out_4));
  Adder Adder (.in_1(A), .in_2(Selector_out_4), .out_3(Sum), .out_4(C_V));

  // Notes on the sheet:
  //   for Subtraction, S = 0
  //   for Addition, S = 1
endmodule

module Half_Adder (
  input  A,
  input  B,
  output P,
  output G
);

  xor xor_1 (P, A, B);
  and and_1 (G, A, B);
endmodule

// 4-bit CLA
module CLA_4_bit (
  input  C0,
  input  G0,
  input  P0,
  input  G1,
  input  P1,
  input  G2,
  input  P2,
  input  G3,
  input  P3,
  output S0,
  output S1,
  output S2,
  output S3,
  output C4
);

  wire and_1_out, and_2_out, and_3_out, and_4_out, and_5_out, and_6_out, and_7_out, and_8_out, and_9_out,
       and_10_out, or_1_out, or_2_out, or_3_out;

  and and_1 (and_1_out, P0, C0);
  and and_2 (and_2_out, G0, P1);
  and and_3 (and_3_out, P1, P0, C0);
  and and_4 (and_4_out, G1, P2);
  and and_5 (and_5_out, P2, P1, G0);
  and and_6 (and_6_out, P2, P1, P0, C0);
  and and_7 (and_7_out, G2, P3);
  and and_8 (and_8_out, P3, G1, P2);
  and and_9 (and_9_out, P3, P2, P1, G0);
  and and_10 (and_10_out, P3, P2, P1, P0, C0);
  or or_1 (or_1_out, G0, and_1_out);
  or or_2 (or_2_out, G1, and_2_out, and_3_out);
  or or_3 (or_3_out, G2, and_4_out, and_5_out, and_6_out);
  or or_4 (C4, G3, and_7_out, and_8_out, and_9_out, and_10_out);
  xor xor_1 (S0, C0, P0);
  xor xor_2 (S1, or_1_out, P1);
  xor xor_3 (S2, or_2_out, P2);
  xor xor_4 (S3, or_3_out, P3);
endmodule

module CLA_16_bit (
  input  [15:0] G,
  input  [15:0] P,
  output [15:0] Sum,
  output C12
);

  wire and_1_out, cla_4_bit_1_c4, cla_4_bit_2_c4, cla_4_bit_3_c4;

  and and_1 (and_1_out, G[0], P[0]);
  CLA_4_bit cla_4_bit_1 (
    .G0(G[0]), .P0(P[0]), .G1(G[1]), .P1(P[1]), .G2(G[2]), .P2(P[2]), .G3(G[3]), .P3(P[3]), .C0(and_1_out),
    .S0(Sum[0]), .S1(Sum[1]), .S2(Sum[2]), .S3(Sum[3]), .C4(cla_4_bit_1_c4));
  CLA_4_bit cla_4_bit_2 (
    .G0(G[4]), .P0(P[4]), .G1(G[5]), .P1(P[5]), .G2(G[6]), .P2(P[6]), .G3(G[7]), .P3(P[7]),
    .C0(cla_4_bit_1_c4), .S0(Sum[4]), .S1(Sum[5]), .S2(Sum[6]), .S3(Sum[7]), .C4(cla_4_bit_2_c4));
  CLA_4_bit cla_4_bit_3 (
    .G0(G[8]), .P0(P[8]), .G1(G[9]), .P1(P[9]), .G2(G[10]), .P2(P[10]), .G3(G[11]), .P3(P[11]),
    .C0(cla_4_bit_2_c4), .S0(Sum[8]), .S1(Sum[9]), .S2(Sum[10]), .S3(Sum[11]), .C4(cla_4_bit_3_c4));
  CLA_4_bit cla_4_bit_4 (
    .G0(G[12]), .P0(P[12]), .G1(G[13]), .P1(P[13]), .G2(G[14]), .P2(P[14]), .G3(G[15]), .P3(P[15]),
    .C0(cla_4_bit_3_c4), .S0(Sum[12]), .S1(Sum[13]), .S2(Sum[14]), .S3(Sum[15]), .C4(C12));
endmodule

module G_and_P (
  input  [15:0] A,
  input  [15:0] B,
  output [15:0] P,
  output [15:0] G
);

  Half_Adder Half_Adder (.A(A[0]), .B(B[0]), .P(P[0]), .G(G[0]));
  Half_Adder half_adder_2 (.A(A[1]), .B(B[1]), .P(P[1]), .G(G[1]));
  Half_Adder half_adder_3 (.A(A[2]), .B(B[2]), .P(P[2]), .G(G[2]));
  Half_Adder half_adder_4 (.A(A[3]), .B(B[3]), .P(P[3]), .G(G[3]));
  Half_Adder half_adder_5 (.A(A[4]), .B(B[4]), .P(P[4]), .G(G[4]));
  Half_Adder half_adder_6 (.A(A[5]), .B(B[5]), .P(P[5]), .G(G[5]));
  Half_Adder half_adder_7 (.A(A[6]), .B(B[6]), .P(P[6]), .G(G[6]));
  Half_Adder half_adder_8 (.A(A[7]), .B(B[7]), .P(P[7]), .G(G[7]));
  Half_Adder half_adder_9 (.A(A[8]), .B(B[8]), .P(P[8]), .G(G[8]));
  Half_Adder half_adder_10 (.A(A[9]), .B(B[9]), .P(P[9]), .G(G[9]));
  Half_Adder half_adder_11 (.A(A[10]), .B(B[10]), .P(P[10]), .G(G[10]));
  Half_Adder half_adder_12 (.A(A[11]), .B(B[11]), .P(P[11]), .G(G[11]));
  Half_Adder half_adder_13 (.A(A[12]), .B(B[12]), .P(P[12]), .G(G[12]));
  Half_Adder half_adder_14 (.A(A[13]), .B(B[13]), .P(P[13]), .G(G[13]));
  Half_Adder half_adder_15 (.A(A[14]), .B(B[14]), .P(P[14]), .G(G[14]));
  Half_Adder half_adder_16 (.A(A[15]), .B(B[15]), .P(P[15]), .G(G[15]));
endmodule

module Adder (
  input  [15:0] in_1,
  input  [15:0] in_2,
  output [15:0] out_3,
  output out_4
);

  wire [15:0] G_and_P_g, G_and_P_p;

  G_and_P G_and_P (.A(in_1), .B(in_2), .P(G_and_P_p), .G(G_and_P_g));
  CLA_16_bit _16_bit_CLA (.G(G_and_P_g), .P(G_and_P_p), .Sum(out_3), .C12(out_4));
endmodule

module _1_s_Complementer (
  input  [15:0] in_1,
  output [15:0] out_2
);

  not not_1 (out_2[0], in_1[0]);
  not not_2 (out_2[1], in_1[1]);
  not not_3 (out_2[2], in_1[2]);
  not not_4 (out_2[3], in_1[3]);
  not not_5 (out_2[4], in_1[4]);
  not not_6 (out_2[5], in_1[5]);
  not not_7 (out_2[6], in_1[6]);
  not not_8 (out_2[7], in_1[7]);
  not not_9 (out_2[8], in_1[8]);
  not not_10 (out_2[9], in_1[9]);
  not not_11 (out_2[10], in_1[10]);
  not not_12 (out_2[11], in_1[11]);
  not not_13 (out_2[12], in_1[12]);
  not not_14 (out_2[13], in_1[13]);
  not not_15 (out_2[14], in_1[14]);
  not not_16 (out_2[15], in_1[15]);
endmodule

module _2_s_Complementer (
  input  [15:0] X,
  input  [15:0] _1,
  output [15:0] Y
);

  wire [15:0] _1_s_Complementer_out_2;

  _1_s_Complementer _1_s_Complementer (.in_1(X), .out_2(_1_s_Complementer_out_2));
  Adder _16_bit_Adder (.in_1(_1_s_Complementer_out_2), .in_2(_1), .out_3(Y));  // open: out_4
endmodule

module Selector (
  input  [15:0] A,
  input  [15:0] B,
  input  Select,
  output [15:0] out_4
);

  wire and_1_out, and_2_out, and_3_out, and_4_out, and_5_out, and_6_out, and_7_out, and_8_out, and_9_out,
       and_10_out, and_11_out, and_12_out, and_13_out, and_14_out, and_15_out, and_16_out, and_17_out,
       and_18_out, and_19_out, and_20_out, and_21_out, and_22_out, and_23_out, and_24_out, and_25_out,
       and_26_out, and_27_out, and_28_out, and_29_out, and_30_out, and_31_out, and_32_out, not_1_out;

  not not_1 (not_1_out, Select);
  and and_1 (and_1_out, Select, A[0]);
  and and_2 (and_2_out, not_1_out, B[0]);
  and and_3 (and_3_out, Select, A[1]);
  and and_4 (and_4_out, not_1_out, B[1]);
  and and_5 (and_5_out, Select, A[2]);
  and and_6 (and_6_out, not_1_out, B[2]);
  and and_7 (and_7_out, Select, A[3]);
  and and_8 (and_8_out, not_1_out, B[3]);
  and and_9 (and_9_out, Select, A[4]);
  and and_10 (and_10_out, not_1_out, B[4]);
  and and_11 (and_11_out, Select, A[5]);
  and and_12 (and_12_out, not_1_out, B[5]);
  and and_13 (and_13_out, Select, A[6]);
  and and_14 (and_14_out, not_1_out, B[6]);
  and and_15 (and_15_out, Select, A[7]);
  and and_16 (and_16_out, not_1_out, B[7]);
  and and_17 (and_17_out, Select, A[8]);
  and and_18 (and_18_out, not_1_out, B[8]);
  and and_19 (and_19_out, Select, A[9]);
  and and_20 (and_20_out, not_1_out, B[9]);
  and and_21 (and_21_out, Select, A[10]);
  and and_22 (and_22_out, not_1_out, B[10]);
  and and_23 (and_23_out, Select, A[11]);
  and and_24 (and_24_out, not_1_out, B[11]);
  and and_25 (and_25_out, Select, A[12]);
  and and_26 (and_26_out, not_1_out, B[12]);
  and and_27 (and_27_out, Select, A[13]);
  and and_28 (and_28_out, not_1_out, B[13]);
  and and_29 (and_29_out, Select, A[14]);
  and and_30 (and_30_out, not_1_out, B[14]);
  and and_31 (and_31_out, Select, A[15]);
  and and_32 (and_32_out, not_1_out, B[15]);
  or or_1 (out_4[0], and_1_out, and_2_out);
  or or_2 (out_4[1], and_3_out, and_4_out);
  or or_3 (out_4[2], and_5_out, and_6_out);
  or or_4 (out_4[3], and_7_out, and_8_out);
  or or_5 (out_4[4], and_9_out, and_10_out);
  or or_6 (out_4[5], and_11_out, and_12_out);
  or or_7 (out_4[6], and_13_out, and_14_out);
  or or_8 (out_4[7], and_15_out, and_16_out);
  or or_9 (out_4[8], and_17_out, and_18_out);
  or or_10 (out_4[9], and_19_out, and_20_out);
  or or_11 (out_4[10], and_21_out, and_22_out);
  or or_12 (out_4[11], and_23_out, and_24_out);
  or or_13 (out_4[12], and_25_out, and_26_out);
  or or_14 (out_4[13], and_27_out, and_28_out);
  or or_15 (out_4[14], and_29_out, and_30_out);
  or or_16 (out_4[15], and_31_out, and_32_out);
endmodule
