// Logisim project Half and Full Adder.circ as structural Verilog
module Half_Adder (
  input  A,
  input  B,
  output Sum,
  output Carry
);

  xor xor_1 (Sum, A, B);
  and and_1 (Carry, A, B);
endmodule

module Full_Adder (
  input  A,
  input  B,
  input  C,
  output Sum,
  output Carry
);

  wire Half_Adder_2_carry, Half_Adder_carry, Half_Adder_sum;

  Half_Adder Half_Adder (.A(A), .B(B), .Sum(Half_Adder_sum), .Carry(Half_Adder_carry));
  Half_Adder Half_Adder_2 (.A(Half_Adder_sum), .B(C), .Sum(Sum), .Carry(Half_Adder_2_carry));
  or or_1 (Carry, Half_Adder_2_carry, Half_Adder_carry);
endmodule

module Half_Subtractor (
  input  A,
  input  B,
  output Difference,
  output Borrow
);

  wire not_1_out;

  not not_1 (not_1_out, A);
  xor xor_1 (Difference, A, B);
  and and_1 (Borrow, not_1_out, B);
endmodule

module Full_Subtractor (
  input  A,
  input  B,
  input  C,
  output Difference,
  output Borrow
);

  wire Half_Subtractor_2_borrow, Half_Subtractor_borrow, Half_Subtractor_difference;

  Half_Subtractor Half_Subtractor (
    .A(A), .B(B), .Difference(Half_Subtractor_difference), .Borrow(Half_Subtractor_borrow));
  Half_Subtractor Half_Subtractor_2 (
    .A(Half_Subtractor_difference), .B(C), .Difference(Difference), .Borrow(Half_Subtractor_2_borrow));
  or or_1 (Borrow, Half_Subtractor_2_borrow, Half_Subtractor_borrow);
endmodule
