// Logisim project Q2.circ as structural Verilog
module _8_bit_AND (
  input  A0,
  input  B0,
  input  A1,
  input  B1,
  input  A2,
  input  B2,
  input  A3,
  input  B3,
  input  A4,
  input  B4,
  input  A5,
  input  B5,
  input  A6,
  input  B6,
  input  A7,
  input  B7,
  output Y0,
  output Y1,
  output Y2,
  output Y3,
  output Y4,
  output Y5,
  output Y6,
  output Y7
);

  and and_1 (Y0, A0, B0);
  and and_2 (Y1, A1, B1);
  and and_3 (Y2, A2, B2);
  and and_4 (Y3, A3, B3);
  and and_5 (Y4, A4, B4);
  and and_6 (Y5, A5, B5);
  and and_7 (Y6, A6, B6);
  and and_8 (Y7, A7, B7);
endmodule

module _8_bit_OR (
  input  A0,
  input  B0,
  input  A1,
  input  B1,
  input  A2,
  input  B2,
  input  A3,
  input  B3,
  input  A4,
  input  B4,
  input  A5,
  input  B5,
  input  A6,
  input  B6,
  input  A7,
  input  B7,
  output Y0,
  output Y1,
  output Y2,
  output Y3,
  output Y4,
  output Y5,
  output Y6,
  output Y7
);

  or or_1 (Y0, A0, B0);
  or or_2 (Y1, A1, B1);
  or or_3 (Y2, A2, B2);
  or or_4 (Y3, A3, B3);
  or or_5 (Y4, A4, B4);
  or or_6 (Y5, A5, B5);
  or or_7 (Y6, A6, B6);
  or or_8 (Y7, A7, B7);
endmodule

module _8_bit_NOT (
  input  A0,
  input  A1,
  input  A2,
  input  A3,
  input  A4,
  input  A5,
  input  A6,
  input  A7,
  output Y0,
  output Y1,
  output Y2,
  output Y3,
  output Y4,
  output Y5,
  output Y6,
  output Y7
);

  not not_1 (Y0, A0);
  not not_2 (Y1, A1);
  not not_3 (Y2, A2);
  not not_4 (Y3, A3);
  not not_5 (Y4, A4);
  not not_6 (Y5, A5);
  not not_7 (Y6, A6);
  not not_8 (Y7, A7);
endmodule

module _8_bit_XOR (
  input  A0,
  input  B0,
  input  A1,
  input  B1,
  input  A2,
  input  B2,
  input  A3,
  input  B3,
  input  A4,
  input  B4,
  input  A5,
  input  B5,
  input  A6,
  input  B6,
  input  A7,
  input  B7,
  output Y0,
  output Y1,
  output Y2,
  output Y3,
  output Y4,
  output Y5,
  output Y6,
  output Y7
);

  xor xor_1 (Y0, A0, B0);
  xor xor_2 (Y1, A1, B1);
  xor xor_3 (Y2, A2, B2);
  xor xor_4 (Y3, A3, B3);
  xor xor_5 (Y4, A4, B4);
  xor xor_6 (Y5, A5, B5);
  xor xor_7 (Y6, A6, B6);
  xor xor_8 (Y7, A7, B7);
endmodule
