// Logisim project Q3.circ as structural Verilog
module _8_bit_AND (
  input  in_1,
  input  A0,
  input  B0,
  input  A1,
  input  B1,
  input  A2,
  input  B2,
  input  A3,
  input  B3,
  input  A4,
  input  B4,
  input  A5,
  input  B5,
  input  A6,
  input  B6,
  input  A7,
  input  B7,
  output Y0,
  output Y1,
  output Y2,
  output Y3,
  output Y4,
  output Y5,
  output Y6,
  output Y7
);

  wire and_1_out, and_2_out, and_3_out, and_4_out, and_5_out, and_6_out, and_7_out, and_8_out;

  and and_1 (and_1_out, A0, B0);
  and and_2 (and_2_out, A1, B1);
  and and_3 (and_3_out, A2, B2);
  and and_4 (and_4_out, A3, B3);
  and and_5 (and_5_out, A4, B4);
  and and_6 (and_6_out, A5, B5);
  and and_7 (and_7_out, A6, B6);
  and and_8 (and_8_out, A7, B7);
  assign Y0 = in_1 ? and_1_out : 1'bz;  // Controlled_Buffer controlled_buffer_1
  assign Y1 = in_1 ? and_2_out : 1'bz;  // Controlled_Buffer controlled_buffer_2
  assign Y2 = in_1 ? and_3_out : 1'bz;  // Controlled_Buffer controlled_buffer_3
  assign Y3 = in_1 ? and_4_out : 1'bz;  // Controlled_Buffer controlled_buffer_4
  assign Y4 = in_1 ? and_5_out : 1'bz;  // Controlled_Buffer controlled_buffer_5
  assign Y5 = in_1 ? and_6_out : 1'bz;  // Controlled_Buffer controlled_buffer_6
  assign Y6 = in_1 ? and_7_out : 1'bz;  // Controlled_Buffer controlled_buffer_7
  assign Y7 = in_1 ? and_8_out : 1'bz;  // Controlled_Buffer controlled_buffer_8
endmodule

module _8_bit_OR (
  input  in_1,
  input  A0,
  input  B0,
  input  A1,
  input  B1,
  input  A2,
  input  B2,
  input  A3,
  input  B3,
  input  A4,
  input  B4,
  input  A5,
  input  B5,
  input  A6,
  input  B6,
  input  A7,
  input  B7,
  output Y0,
  output Y1,
  output Y2,
  output Y3,
  output Y4,
  output Y5,
  output Y6,
  output Y7
);

  wire or_1_out, or_2_out, or_3_out, or_4_out, or_5_out, or_6_out, or_7_out, or_8_out;

  or or_1 (or_1_out, A0, B0);
  or or_2 (or_2_out, A1, B1);
  or or_3 (or_3_out, A2, B2);
  or or_4 (or_4_out, A3, B3);
  or or_5 (or_5_out, A4, B4);
  or or_6 (or_6_out, A5, B5);
  or or_7 (or_7_out, A6, B6);
  or or_8 (or_8_out, A7, B7);
  assign Y0 = in_1 ? or_1_out : 1'bz;  // Controlled_Buffer controlled_buffer_1
  assign Y1 = in_1 ? or_2_out : 1'bz;  // Controlled_Buffer controlled_buffer_2
  assign Y2 = in_1 ? or_3_out : 1'bz;  // Controlled_Buffer controlled_buffer_3
  assign Y3 = in_1 ? or_4_out : 1'bz;  // Controlled_Buffer controlled_buffer_4
  assign Y4 = in_1 ? or_5_out : 1'bz;  // Controlled_Buffer controlled_buffer_5
  assign Y5 = in_1 ? or_6_out : 1'bz;  // Controlled_Buffer controlled_buffer_6
  assign Y6 = in_1 ? or_7_out : 1'bz;  // Controlled_Buffer controlled_buffer_7
  assign Y7 = in_1 ? or_8_out : 1'bz;  // Controlled_Buffer controlled_buffer_8
endmodule

module _8_bit_NOT (
  input  in_1,
  input  A0,
  input  A1,
  input  A2,
  input  A3,
  input  A4,
  input  A5,
  input  A6,
  input  A7,
  output Y0,
  output Y1,
  output Y2,
  output Y3,
  output Y4,
  output Y5,
  output Y6,
  output Y7
);

  wire not_1_out, not_2_out, not_3_out, not_4_out, not_5_out, not_6_out, not_7_out, not_8_out;

  not not_1 (not_1_out, A0);
  not not_2 (not_2_out, A1);
  not not_3 (not_3_out, A2);
  not not_4 (not_4_out, A3);
  not not_5 (not_5_out, A4);
  not not_6 (not_6_out, A5);
  not not_7 (not_7_out, A6);
  not not_8 (not_8_out, A7);
  assign Y0 = in_1 ? not_1_out : 1'bz;  // Controlled_Buffer controlled_buffer_1
  assign Y1 = in_1 ? not_2_out : 1'bz;  // Controlled_Buffer controlled_buffer_2
  assign Y2 = in_1 ? not_3_out : 1'bz;  // Controlled_Buffer controlled_buffer_3
  assign Y3 = in_1 ? not_4_out : 1'bz;  // Controlled_Buffer controlled_buffer_4
  assign Y4 = in_1 ? not_5_out : 1'bz;  // Controlled_Buffer controlled_buffer_5
  assign Y5 = in_1 ? not_6_out : 1'bz;  // Controlled_Buffer controlled_buffer_6
  assign Y6 = in_1 ? not_7_out : 1'bz;  // Controlled_Buffer controlled_buffer_7
  assign Y7 = in_1 ? not_8_out : 1'bz;  // Controlled_Buffer controlled_buffer_8
endmodule

module _8_bit_XOR (
  input  in_1,
  input  A0,
  input  B0,
  input  A1,
  input  B1,
  input  A2,
  input  B2,
  input  A3,
  input  B3,
  input  A4,
  input  B4,
  input  A5,
  input  B5,
  input  A6,
  input  B6,
  input  A7,
  input  B7,
  output Y0,
  output Y1,
  output Y2,
  output Y3,
  output Y4,
  output Y5,
  output Y6,
  output Y7
);

  wire xor_1_out, xor_2_out, xor_3_out, xor_4_out, xor_5_out, xor_6_out, xor_7_out, xor_8_out;

  xor xor_1 (xor_1_out, A0, B0);
  xor xor_2 (xor_2_out, A1, B1);
  xor xor_3 (xor_3_out, A2, B2);
  xor xor_4 (xor_4_out, A3, B3);
  xor xor_5 (xor_5_out, A4, B4);
  xor xor_6 (xor_6_out, A5, B5);
  xor xor_7 (xor_7_out, A6, B6);
  xor xor_8 (xor_8_out, A7, B7);
  assign Y0 = in_1 ? xor_1_out : 1'bz;  // Controlled_Buffer controlled_buffer_1
  assign Y1 = in_1 ? xor_2_out : 1'bz;  // Controlled_Buffer controlled_buffer_2
  assign Y2 = in_1 ? xor_3_out : 1'bz;  // Controlled_Buffer controlled_buffer_3
  assign Y3 = in_1 ? xor_4_out : 1'bz;  // Controlled_Buffer controlled_buffer_4
  assign Y4 = in_1 ? xor_5_out : 1'bz;  // Controlled_Buffer controlled_buffer_5
  assign Y5 = in_1 ? xor_6_out : 1'bz;  // Controlled_Buffer controlled_buffer_6
  assign Y6 = in_1 ? xor_7_out : 1'bz;  // Controlled_Buffer controlled_buffer_7
  assign Y7 = in_1 ? xor_8_out : 1'bz;  // Controlled_Buffer controlled_buffer_8
endmodule
