// Logisim project Q4.circ as structural Verilog: 1 circuit, main circuit main
module main (
  input  S2,
  input  S1,
  input  A,
  input  B,
  input  C,
  input  D,
  output Y
);

  wire nand_1_out, nand_2_out, nand_3_out, nand_4_out, nand_5_out, nand_6_out;

  nand nand_1 (nand_1_out, S2, S2);
  nand nand_2 (nand_2_out, S1, S1);
  nand nand_3 (nand_3_out, A, nand_1_out, nand_2_out);
  nand nand_4 (nand_4_out, B, S2, nand_2_out);
  nand nand_5 (nand_5_out, C, nand_1_out, S1);
  nand nand_6 (nand_6_out, D, S2, S1);
  nand nand_7 (Y, nand_3_out, nand_4_out, nand_5_out, nand_6_out);
endmodule
