// Logisim project Q5.circ as structural Verilog: 1 circuit, main circuit main
module main (
  input  S0,
  input  S1,
  input  [7:0] A,
  input  [7:0] B,
  output [7:0] Y
);

  wire and_1_out, and_2_out, and_3_out, and_4_out, and_5_out, and_6_out, and_7_out, and_8_out, and_9_out,
       and_10_out, and_11_out, and_12_out, and_13_out, and_14_out, and_15_out, and_16_out, and_17_out,
       and_18_out, and_19_out, and_20_out, and_21_out, and_22_out, and_23_out, and_24_out, and_25_out,
       and_26_out, and_27_out, and_28_out, and_29_out, and_30_out, and_31_out, and_32_out, and_33_out,
       and_34_out, and_35_out, and_36_out, and_37_out, and_38_out, and_39_out, and_40_out, not_1_out,
       not_2_out, not_3_out, not_4_out, not_5_out, not_6_out, not_7_out, not_8_out, not_9_out, not_10_out,
       or_1_out, or_2_out, or_3_out, or_4_out, or_5_out, or_6_out, or_7_out, or_8_out, xor_1_out, xor_2_out,
       xor_3_out, xor_4_out, xor_5_out, xor_6_out, xor_7_out, xor_8_out;

  and and_1 (and_1_out, B[0], A[0]);
  or or_1 (or_1_out, B[0], A[0]);
  xor xor_1 (xor_1_out, B[0], A[0]);
  not not_1 (not_1_out, A[0]);
  and and_2 (and_2_out, B[1], A[1]);
  or or_2 (or_2_out, B[1], A[1]);
  xor xor_2 (xor_2_out, B[1], A[1]);
  not not_2 (not_2_out, A[1]);
  and and_3 (and_3_out, B[2], A[2]);
  or or_3 (or_3_out, B[2], A[2]);
  xor xor_3 (xor_3_out, B[2], A[2]);
  not not_3 (not_3_out, A[2]);
  and and_4 (and_4_out, B[3], A[3]);
  or or_4 (or_4_out, B[3], A[3]);
  xor xor_4 (xor_4_out, B[3], A[3]);
  not not_4 (not_4_out, A[3]);
  and and_5 (and_5_out, B[4], A[4]);
  or or_5 (or_5_out, B[4], A[4]);
  xor xor_5 (xor_5_out, B[4], A[4]);
  not not_5 (not_5_out, A[4]);
  and and_6 (and_6_out, B[5], A[5]);
  or or_6 (or_6_out, B[5], A[5]);
  xor xor_6 (xor_6_out, B[5], A[5]);
  not not_6 (not_6_out, A[5]);
  and and_7 (and_7_out, B[6], A[6]);
  or or_7 (or_7_out, B[6], A[6]);
  xor xor_7 (xor_7_out, B[6], A[6]);
  not not_7 (not_7_out, A[6]);
  and and_8 (and_8_out, B[7], A[7]);
  or or_8 (or_8_out, B[7], A[7]);
  xor xor_8 (xor_8_out, B[7], A[7]);
  not not_8 (not_8_out, A[7]);
  not not_9 (not_9_out, S0);
  not not_10 (not_10_out, S1);
  and and_9 (and_9_out, S0, S1, and_1_out);
  and and_10 (and_10_out, not_9_out, not_10_out, or_1_out);
  and and_11 (and_11_out, S1, not_9_out, xor_1_out);
  and and_12 (and_12_out, not_10_out, S0, not_1_out);
  and and_13 (and_13_out, S0, S1, and_2_out);
  and and_14 (and_14_out, not_9_out, not_10_out, or_2_out);
  and and_15 (and_15_out, S1, not_9_out, xor_2_out);
  and and_16 (and_16_out, not_10_out, S0, not_2_out);
  and and_17 (and_17_out, S0, S1, and_3_out);
  and and_18 (and_18_out, not_9_out, not_10_out, or_3_out);
  and and_19 (and_19_out, S1, not_9_out, xor_3_out);
  and and_20 (and_20_out, not_10_out, S0, not_3_out);
  and and_21 (and_21_out, S0, S1, and_4_out);
  and and_22 (and_22_out, not_9_out, not_10_out, or_4_out);
  and and_23 (and_23_out, S1, not_9_out, xor_4_out);
  and and_24 (and_24_out, not_10_out, S0, not_4_out);
  and and_25 (and_25_out, S0, S1, and_5_out);
  and and_26 (and_26_out, not_9_out, not_10_out, or_5_out);
  and and_27 (and_27_out, S1, not_9_out, xor_5_out);
  and and_28 (and_28_out, not_10_out, S0, not_5_out);
  and and_29 (and_29_out, S0, S1, and_6_out);
  and and_30 (and_30_out, not_9_out, not_10_out, or_6_out);
  and and_31 (and_31_out, S1, not_9_out, xor_6_out);
  and and_32 (and_32_out, not_10_out, S0, not_6_out);
  and and_33 (and_33_out, S0, S1, and_7_out);
  and and_34 (and_34_out, not_9_out, not_10_out, or_7_out);
  and and_35 (and_35_out, S1, not_9_out, xor_7_out);
  and and_36 (and_36_out, not_10_out, S0, not_7_out);
  and and_37 (and_37_out, S0, S1, and_8_out);
  and and_38 (and_38_out, not_9_out, not_10_out, or_8_out);
  and and_39 (and_39_out, S1, not_9_out, xor_8_out);
  and and_40 (and_40_out, not_10_out, S0, not_8_out);
  or or_9 (Y[0], and_9_out, and_10_out, and_11_out, and_12_out);
  or or_10 (Y[1], and_13_out, and_14_out, and_15_out, and_16_out);
  or or_11 (Y[2], and_17_out, and_18_out, and_19_out, and_20_out);
  or or_12 (Y[3], and_21_out, and_22_out, and_23_out, and_24_out);
  or or_13 (Y[4], and_25_out, and_26_out, and_27_out, and_28_out);
  or or_14 (Y[5], and_29_out, and_30_out, and_31_out, and_32_out);
  or or_15 (Y[6], and_33_out, and_34_out, and_35_out, and_36_out);
  or or_16 (Y[7], and_37_out, and_38_out, and_39_out, and_40_out);

  // Notes on the sheet:
  //   AND Logic: S0 = 1, S1 = 1
  //   OR Logic: S0 = 0, S1 = 0
  //   XOR Logic: S0 = 0, S1 = 1
  //   NOT(of A) Logic: S0 = 1, S1 = 0
endmodule
