// Logisim project Q6.circ as structural Verilog: 2 circuits, main circuit main
module main (
  input  [1:0] Shift_Count,
  input  X0,
  input  X1,
  input  X2,
  input  X3,
  output Y3,
  output Y2,
  output Y1,
  output Y0
);

  wire _4_bit_Decoder_y0, _4_bit_Decoder_y1, _4_bit_Decoder_y2, _4_bit_Decoder_y3;

  Decoder _4_bit_Decoder (
    .S1(Shift_Count[1]), .S0(Shift_Count[0]), .Y0(_4_bit_Decoder_y0), .Y1(_4_bit_Decoder_y1),
    .Y2(_4_bit_Decoder_y2), .Y3(_4_bit_Decoder_y3));
  assign Y3 = _4_bit_Decoder_y3 ? X0 : 1'bz;  // Controlled_Buffer controlled_buffer_1
  assign Y2 = _4_bit_Decoder_y2 ? X0 : 1'bz;  // Controlled_Buffer controlled_buffer_2
  assign Y1 = _4_bit_Decoder_y1 ? X0 : 1'bz;  // Controlled_Buffer controlled_buffer_3
  assign Y0 = _4_bit_Decoder_y0 ? X0 : 1'bz;  // Controlled_Buffer controlled_buffer_4
  assign Y3 = _4_bit_Decoder_y2 ? X1 : 1'bz;  // Controlled_Buffer controlled_buffer_5
  assign Y2 = _4_bit_Decoder_y1 ? X1 : 1'bz;  // Controlled_Buffer controlled_buffer_6
  assign Y1 = _4_bit_Decoder_y0 ? X1 : 1'bz;  // Controlled_Buffer controlled_buffer_7
  assign Y0 = _4_bit_Decoder_y3 ? X1 : 1'bz;  // Controlled_Buffer controlled_buffer_8
  assign Y3 = _4_bit_Decoder_y0 ? X3 : 1'bz;  // Controlled_Buffer controlled_buffer_9
  assign Y3 = _4_bit_Decoder_y1 ? X2 : 1'bz;  // Controlled_Buffer controlled_buffer_10
  assign Y2 = _4_bit_Decoder_y0 ? X2 : 1'bz;  // Controlled_Buffer controlled_buffer_11
  assign Y2 = _4_bit_Decoder_y3 ? X3 : 1'bz;  // Controlled_Buffer controlled_buffer_12
  assign Y1 = _4_bit_Decoder_y2 ? X3 : 1'bz;  // Controlled_Buffer controlled_buffer_13
  assign Y1 = _4_bit_Decoder_y3 ? X2 : 1'bz;  // Controlled_Buffer controlled_buffer_14
  assign Y0 = _4_bit_Decoder_y1 ? X3 : 1'bz;  // Controlled_Buffer controlled_buffer_15
  assign Y0 = _4_bit_Decoder_y2 ? X2 : 1'bz;  // Controlled_Buffer controlled_buffer_16
endmodule

module Decoder (
  input  S1,
  input  S0,
  output Y0,
  output Y1,
  output Y2,
  output Y3
);

  wire not_1_out, not_2_out;

  not not_1 (not_1_out, S1);
  not not_2 (not_2_out, S0);
  and and_1 (Y0, not_2_out, not_1_out);
  and and_2 (Y1, not_1_out, S0);
  and and_3 (Y2, S1, not_2_out);
  and and_4 (Y3, S1, S0);
endmodule
